// Logisim project main.circ as structural Verilog: 3 circuits, main circuit Magnitude-Comparator
// Is full?
module Magnitude_Comparator (
  input  in_1,
  input  in_2,
  input  in_3,
  input  in_4,
  input  in_5,
  input  in_6,
  input  in_7,
  input  in_8,
  output out_9
);

  wire xnor_1_out, xnor_2_out, xnor_3_out, xnor_4_out;

  xnor xnor_1 (xnor_1_out, in_1, in_2);
  xnor xnor_2 (xnor_2_out, in_3, in_4);
  xnor xnor_3 (xnor_3_out, in_5, in_6);
  xnor xnor_4 (xnor_4_out, in_7, in_8);
  and and_1 (out_9, xnor_1_out, xnor_2_out, xnor_3_out, xnor_4_out);
endmodule

// Counter
module Up_Down_Counter (
  input  Up_Down_prime,
  input  Reset,
  output LSB,
  output out_4,
  output out_5,
  output MSB
);

  wire and_1_out, and_2_out, and_3_out, and_4_out, and_5_out, and_6_out, CLK_out, j_k_ff_1_qn, j_k_ff_2_qn,
       j_k_ff_3_qn, not_1_out, or_1_out, or_2_out, or_3_out;

  Clock CLK (.out(CLK_out));
  not not_1 (not_1_out, Up_Down_prime);
  J_K_Flip_Flop j_k_ff_1 (
    .J(1'b1), .clk(CLK_out), .K(1'b1), .Q(LSB), .Qn(j_k_ff_1_qn), .reset(Reset));  // open: preset, en
  and and_1 (and_1_out, Up_Down_prime, LSB);
  and and_2 (and_2_out, j_k_ff_1_qn, not_1_out, not_1_out);
  or or_1 (or_1_out, and_1_out, and_2_out);
  J_K_Flip_Flop j_k_ff_2 (
    .J(or_1_out), .clk(CLK_out), .K(or_1_out), .Q(out_4), .Qn(j_k_ff_2_qn), .reset(Reset));  // open: preset, en
  and and_3 (and_3_out, and_1_out, out_4);
  and and_4 (and_4_out, j_k_ff_2_qn, and_2_out);
  or or_2 (or_2_out, and_3_out, and_4_out);
  J_K_Flip_Flop j_k_ff_3 (
    .J(or_2_out), .clk(CLK_out), .K(or_2_out), .Q(out_5), .Qn(j_k_ff_3_qn), .reset(Reset));  // open: preset, en
  and and_5 (and_5_out, and_3_out, out_5);
  and and_6 (and_6_out, j_k_ff_3_qn, and_4_out);
  or or_3 (or_3_out, and_5_out, and_6_out);
  J_K_Flip_Flop j_k_ff_4 (.J(or_3_out), .clk(CLK_out), .K(or_3_out), .Q(MSB), .reset(Reset));  // open: Qn, preset, en
endmodule

module Main_Area (
  input  _1_Up_0_Down,
  output MSB,
  output out_3,
  output out_4,
  output LSB
);

  wire magnitude_comparator_1_out_9;

  Magnitude_Comparator magnitude_comparator_1 (
    .in_1(1'b1), .in_2(LSB), .in_3(1'b1), .in_4(out_4), .in_5(1'b1), .in_6(out_3), .in_7(1'b1), .in_8(MSB),
    .out_9(magnitude_comparator_1_out_9));
  Up_Down_Counter up_down_counter_1 (
    .Up_Down_prime(_1_Up_0_Down), .LSB(LSB), .out_4(out_4), .out_5(out_3), .MSB(MSB));  // open: Reset
  LED led_1 (.in(magnitude_comparator_1_out_9));

  // Notes on the sheet:
  //   Use CTRL+T to run a clock pulse 
endmodule
